// Logisim project exp6.circ as structural Verilog: 1 circuit, main circuit main
module main (
  input  [4:0] in_1,
  input  [3:0] in_2,
  input  [3:0] in_3,
  input  in_4,
  input  in_5,
  input  in_6,
  input  [1:0] in_7,
  input  in_8,
  input  in_9,
  input  in_10,
  input  in_11,
  input  [1:0] in_12,
  input  in_13,
  input  in_14,
  input  in_15,
  input  [1:0] in_16,
  input  in_17,
  input  in_18,
  input  in_19,
  input  in_20,
  input  [1:0] in_21,
  input  in_22,
  input  in_23,
  input  in_24,
  input  [1:0] in_25,
  input  in_26,
  input  in_27,
  input  in_28,
  input  in_29,
  input  [1:0] in_30,
  input  in_31,
  input  in_32,
  output out_33,
  output out_34,
  output out_35,
  output out_36,
  output out_37,
  output out_38,
  output out_39,
  output out_40
);

  wire adder_1_out, adder_2_out, adder_3_out, adder_4_out, and_1_out, and_2_out, and_3_out, and_4_out,
       multiplexer_1_out, multiplexer_2_out, multiplexer_3_out, multiplexer_4_out, multiplexer_5_out,
       multiplexer_6_out, multiplexer_7_out, multiplexer_8_out, not_1_out, not_2_out, not_3_out, not_4_out,
       not_5_out, not_6_out, not_7_out, not_8_out, not_9_out, not_10_out, not_11_out, not_12_out, or_1_out,
       or_2_out, or_3_out, or_4_out, undriven, undriven_2, xor_1_out, xor_2_out, xor_3_out, xor_4_out;
  wire [1:1] undriven_3;

  not not_1 (not_1_out, in_2[0]);
  not not_2 (not_2_out, undriven);
  not not_3 (not_3_out, in_9);
  not not_4 (not_4_out, in_10);
  not not_5 (not_5_out, in_18);
  not not_6 (not_6_out, in_19);
  not not_7 (not_7_out, in_27);
  not not_8 (not_8_out, in_28);
  not not_9 (not_9_out, in_2[0]);
  not not_10 (not_10_out, in_8);
  not not_11 (not_11_out, in_17);
  not not_12 (not_12_out, in_26);
  Multiplexer #(.select(2)) multiplexer_1 (
    .in0(in_2[0]), .in1(not_1_out), .in2(undriven), .in3(not_2_out), .out(multiplexer_1_out),
    .sel({undriven_3[1], in_1[1]}), .en(undriven_2));
  buf and_1 (and_1_out, in_2[0]);  // AND_Gate
  or or_1 (or_1_out, in_2[0], in_2[0]);
  xor xor_1 (xor_1_out, in_2[0], in_2[0]);
  Multiplexer #(.select(2)) multiplexer_2 (
    .in0(in_9), .in1(not_3_out), .in2(in_10), .in3(not_4_out), .out(multiplexer_2_out), .sel(in_7), .en(in_11));
  buf and_2 (and_2_out, in_8);  // AND_Gate
  or or_2 (or_2_out, in_8, in_9);
  xor xor_2 (xor_2_out, in_8, in_9);
  Multiplexer #(.select(2)) multiplexer_3 (
    .in0(in_18), .in1(not_5_out), .in2(in_19), .in3(not_6_out), .out(multiplexer_3_out), .sel(in_16),
    .en(in_20));
  buf and_3 (and_3_out, in_17);  // AND_Gate
  or or_3 (or_3_out, in_17, in_18);
  xor xor_3 (xor_3_out, in_17, in_18);
  Multiplexer #(.select(2)) multiplexer_4 (
    .in0(in_27), .in1(not_7_out), .in2(in_28), .in3(not_8_out), .out(multiplexer_4_out), .sel(in_25),
    .en(in_29));
  buf and_4 (and_4_out, in_26);  // AND_Gate
  or or_4 (or_4_out, in_26, in_27);
  xor xor_4 (xor_4_out, in_26, in_27);
  Adder #(.width(1)) adder_1 (.a(in_2[0]), .b(multiplexer_1_out), .out(adder_1_out), .cin(in_1[0]), .cout(out_34));
  Adder #(.width(1)) adder_2 (.a(in_8), .b(multiplexer_2_out), .out(adder_2_out), .cin(in_6), .cout(out_36));
  Adder #(.width(1)) adder_3 (.a(in_17), .b(multiplexer_3_out), .out(adder_3_out), .cin(in_15), .cout(out_38));
  Adder #(.width(1)) adder_4 (.a(in_26), .b(multiplexer_4_out), .out(adder_4_out), .cin(in_24), .cout(out_40));
  Multiplexer #(.select(2)) multiplexer_5 (
    .in0(and_1_out), .in1(or_1_out), .in2(xor_1_out), .in3(not_9_out), .out(multiplexer_5_out),
    .sel({undriven_3[1], in_1[1]}), .en(undriven_2));
  Multiplexer #(.select(2)) multiplexer_6 (
    .in0(and_2_out), .in1(or_2_out), .in2(xor_2_out), .in3(not_10_out), .out(multiplexer_6_out), .sel(in_7),
    .en(in_11));
  Multiplexer #(.select(2)) multiplexer_7 (
    .in0(and_3_out), .in1(or_3_out), .in2(xor_3_out), .in3(not_11_out), .out(multiplexer_7_out), .sel(in_16),
    .en(in_20));
  Multiplexer #(.select(2)) multiplexer_8 (
    .in0(and_4_out), .in1(or_4_out), .in2(xor_4_out), .in3(not_12_out), .out(multiplexer_8_out), .sel(in_25),
    .en(in_29));
  Multiplexer #(.select(2)) multiplexer_9 (
    .in0(adder_1_out), .in1(multiplexer_5_out), .in2(in_4), .in3(in_5), .out(out_33), .en(undriven_2));  // open: sel
  Multiplexer #(.select(2)) multiplexer_10 (
    .in0(adder_2_out), .in1(multiplexer_6_out), .in2(in_13), .in3(in_14), .out(out_35), .en(in_11));  // open: sel
  Multiplexer #(.select(2)) multiplexer_11 (
    .in0(adder_3_out), .in1(multiplexer_7_out), .in2(in_22), .in3(in_23), .out(out_37), .en(in_20));  // open: sel
  Multiplexer #(.select(2)) multiplexer_12 (
    .in0(adder_4_out), .in1(multiplexer_8_out), .in2(in_31), .in3(in_32), .out(out_39), .en(in_29));  // open: sel
  // Pins of 2 and 4 bits meet at {in_3[3:1], in_2[0]}
  // Pins of 2 and 4 bits meet at in_2
  // Pins of 2 and 5 bits meet at in_1

  assign in_3[0] = in_2[0];
endmodule
